# Fritzing sketch Güvenlik Sistemi (saved by Fritzing 0.9.3b)
breadboards: 1

parts:
  Parça1 = Arduino Uno (Rev3)
  LED1 = LED - 5mm [color="Red (633nm)" package="5 mm [THT]"]
  LED2 = LED - 5mm [color="Green (570nm)" package="5 mm [THT]"]
  R1 = Resistor [tolerance=±5% resistance=220 package="0603 [SMD]"]
  R2 = Resistor [tolerance=±5% resistance=220 package="0603 [SMD]"]
  J1 = Piezo Speaker
  J2 = Basic Servo
  Matrix_keypad1 = KEYPAD 4x4
  LCD1 = LCD screen
  LCM1602_IIC1 = LCM1602 IIC [part_number="LCM1602 IIC" chip_label="LCM1602 IIC" package="DIP (Dual Inline) [THT]"]

nets:
  N1: Parça1.A4/SDA, LCM1602_IIC1.SDA
  N2: Parça1.A5/SCL, LCM1602_IIC1.SCL
  N3: Parça1.D8, Matrix_keypad1.col2
  N4: Parça1.D9_PWM, Matrix_keypad1.col1
  N5: Parça1.D10_PWM/SS, R1.Pin_1
  N6: Parça1.D11_PWM/MOSI, R2.Pin_1
  N7: Parça1.D12/MISO, J1.pin2
  N8: Parça1.D13/SCK, J2.pulse
  GND: Parça1.GND, LED1.cathode, LED2.cathode, J1.pin1, J2.gnd, LCM1602_IIC1.GND
  N9: Parça1.D2, Matrix_keypad1.row4
  N10: Parça1.D3_PWM, Matrix_keypad1.row3
  N11: Parça1.D4, Matrix_keypad1.row2
  N12: Parça1.D5_PWM, Matrix_keypad1.row1
  N13: Parça1.D6_PWM, Matrix_keypad1.col4
  N14: Parça1.D7, Matrix_keypad1.col3
  5V: Parça1.5V, J2.vcc
  N15: LED1.anode, R1.Pin_0
  N16: LED2.anode, R2.Pin_0
  VSS: LCD1.VSS, LCM1602_IIC1.VSS
  VDD: LCD1.VDD, LCM1602_IIC1.VDD
  N17: LCD1.V0, LCM1602_IIC1.V0
  N18: LCD1.RS, LCM1602_IIC1.RS
  N19: LCD1.R/W, LCM1602_IIC1.RW
  N20: LCD1.E, LCM1602_IIC1.E
  N21: LCD1.DB0, LCM1602_IIC1.D0
  N22: LCD1.DB1, LCM1602_IIC1.D1
  N23: LCD1.DB2, LCM1602_IIC1.D2
  N24: LCD1.DB3, LCM1602_IIC1.D3
  N25: LCD1.DB4, LCM1602_IIC1.D4
  N26: LCD1.DB5, LCM1602_IIC1.D5
  N27: LCD1.DB6, LCM1602_IIC1.D6
  N28: LCD1.DB7, LCM1602_IIC1.D7
  N29: LCD1.LED+, LCM1602_IIC1.A
  N30: LCD1.LED-, LCM1602_IIC1.K
  N31: LCM1602_IIC1.LED_A, LCM1602_IIC1.LED_B

custom parts:
  KEYPAD 4x4: Matrix keypad 16 buttons, 4 rows x 4 columns
  LCM1602 IIC: I2C-Module to use a 1602 or 2004 LCD on with the wire.h libory Serial LCD Modul
